# Fritzing sketch AssetTracker (saved by Fritzing 0.9.3b)
breadboards: 1

parts:
  U1 = lolin
  Q1 = MOSFET-NCHANNEL [package=to220v]
  SIM800L_BO1 = SIM800L BO
  D1 = Diode [package=diode-1n4001]
  R1 = Resistor [tolerance=±5% resistance=1k package=THT]
  GY-NEO6MV2 = SUP500F [package=sup500f]
  R2 = Resistor [tolerance=±5% resistance=220 package=THT]
  R3 = Resistor [tolerance=±5% resistance=220 package=THT]
  LED2 = smd LED [color="Green (555nm)" package="0603 [SMD]"]
  LED1 = smd LED [color="Blue (430nm)" package="0603 [SMD]"]
  R4 = Resistor [tolerance=±5% resistance=10k package=THT]

nets:
  N1: U1.connector4, R2.Pin_0
  N2: U1.connector5, R3.Pin_0
  N3: U1.connector8, SIM800L_BO1.pin_5
  N4: U1.connector9, SIM800L_BO1.pin_4
  N5: U1.connector11, R4.Pin_1
  N6: U1.connector14, D1.A, R4.Pin_0
  N7: U1.connector15, Q1.S, LED2.cathode, LED1.cathode
  N8: U1.connector23, GY-NEO6MV2.TX-O
  N9: U1.connector24, GY-NEO6MV2.RX-I
  N10: U1.connector34, GY-NEO6MV2.VCC
  N11: U1.connector37, GY-NEO6MV2.GND
  N12: Q1.G, R1.Pin_1
  N13: Q1.D, SIM800L_BO1.pin_6
  N14: SIM800L_BO1.PIN2, D1.C
  N15: R2.Pin_1, LED1.anode
  N16: R3.Pin_1, LED2.anode

notes:
  GND
  5V
  GND
  3.3V
  UART1
  PIN25 TX1 -> SIM800L RX
  PIN26 RX1 -> SIM800L TX
  UART2
  PIN17 RX2 -> GPS TX
  PIN16 TX2 -> GPS RX
  Status LED
  PIN32 GSM STATUS LED
  PIN33 GPS STATUS LED
  IRF540N MOSFET
  Turn ON/OFF GSM Module
  Add diode to drop voltage
  5v -> 4.2~4.3V
  GSM ANTENNA
